// Logisim project cpu.circ as structural Verilog: 6 circuits, main circuit main
// CPU
module main (
  input  [31:0] RS_READ_VALUE,
  input  [31:0] INSTRUCTION,
  input  [31:0] RI_READ_VALUE,
  input  [31:0] RD_READ_VALUE,
  input  [31:0] JC_READ_VALUE,
  input  CLOCK,
  output [4:0] RS,
  output [4:0] RI,
  output [23:0] FETCH_ADDRESS,
  output [4:0] RD,
  output [31:0] RD_WRITE_VALUE,
  output RD_WRITE_ENABLE
);

  wire u_control_1_alu_src, u_decode_1_i;
  wire [2:0] u_decode_1_jc;
  wire [3:0] u_control_1_alu_control, u_decode_1_op;
  wire [16:0] Imm;
  wire [31:0] bit_extender_1_out, multiplexer_1_out, u_alu_1_alu_result;

  u_decode u_decode_1 (
    .in_1(INSTRUCTION), .OP(u_decode_1_op), .JC(u_decode_1_jc), .I(u_decode_1_i), .RD(RD), .RS(RS), .RI(RI),
    .Immediate(Imm));  // open: Addr
  u_control u_control_1 (
    .OP(u_decode_1_op), .JC(u_decode_1_jc), .I(u_decode_1_i), .ALU_Control(u_control_1_alu_control),
    .ALU_Src(u_control_1_alu_src));  // open: JC_2, J_Src
  Multiplexer #(.width(32), .enable("false")) multiplexer_1 (
    .in0(RI_READ_VALUE), .in1(bit_extender_1_out), .out(multiplexer_1_out), .sel(u_control_1_alu_src));
  assign bit_extender_1_out = {{15{Imm[16]}}, Imm};  // Bit_Extender bit_extender_1
  // Probe on u_alu_1_alu_result
  u_ALU u_alu_1 (
    .ALU_X(RS_READ_VALUE), .ALU_Y(multiplexer_1_out), .ALU_RESULT(u_alu_1_alu_result),
    .ALU_CONTROL(u_control_1_alu_control));
  u_MEM u_mem_1 ();  // open: ADDRESS, WORD_MODE, MEM_WRITE, DATA_IN, CLOCK, DATA_OUT

  // Other names for the same wires on the sheet: CLK = CLOCK
endmodule

module u_ALU (
  input  [3:0] ALU_CONTROL,
  input  [31:0] ALU_X,
  input  [31:0] ALU_Y,
  output [31:0] ALU_RESULT
);

  wire and_2_out, bit_extender_4_out, comparator_1_eq, comparator_2_gt;
  wire [4:0] bit_extender_1_out, bit_extender_2_out, bit_extender_3_out;
  wire [31:0] _00_SL, _01_SR, _02_And, _03_OR, _04_REV, _05_XOR, _06_ADD, _07_SUB, _08_MUL, _09_DIV,
       bit_extender_5_out, multiplexer_1_out, shifter_2_out, shifter_3_out, subtractor_2_out;

  Bit_Extender #(.in_width(32), .out_width(5)) bit_extender_1 (.in(ALU_Y), .out(bit_extender_1_out));
  Bit_Extender #(.in_width(32), .out_width(5)) bit_extender_2 (.in(ALU_Y), .out(bit_extender_2_out));
  assign _02_And = ALU_X & ALU_Y;  // AND_Gate and_1, 32 bits wide
  assign _03_OR = ALU_X | ALU_Y;  // OR_Gate or_1, 32 bits wide
  Bit_Extender #(.in_width(32), .out_width(5)) bit_extender_3 (.in(ALU_Y), .out(bit_extender_3_out));
  assign _05_XOR = ALU_X ^ ALU_Y;  // XOR_Gate xor_1, 32 bits wide
  Adder #(.width(32)) adder_1 (.a(ALU_X), .b(ALU_Y), .out(_06_ADD));  // open: cin, cout
  Subtractor #(.width(32)) subtractor_1 (.a(ALU_X), .b(ALU_Y), .out(_07_SUB));  // open: bin, bout
  Multiplier #(.width(32)) multiplier_1 (.a(ALU_X), .b(ALU_Y), .out(_08_MUL));  // open: cin, cout
  Divider #(.width(32)) divider_1 (.a(ALU_X), .b(ALU_Y), .out(_09_DIV));  // open: upper, rem
  Bit_Extender #(.in_width(32), .out_width(1)) bit_extender_4 (.in(ALU_X), .out(bit_extender_4_out));
  assign bit_extender_5_out = {{31{1'b0}}, bit_extender_4_out};  // Bit_Extender bit_extender_5
  Shifter #(.width(32), .shift("ar")) shifter_1 (.in(ALU_X), .\dist (bit_extender_2_out), .out(_01_SR));
  u_REV u_rev_1 (.INPUT(ALU_X), .REVERSE_AMOUNT(bit_extender_3_out), .OUTPUT(_04_REV));
  Shifter #(.width(32)) shifter_2 (.in(bit_extender_5_out), .\dist (bit_extender_1_out), .out(shifter_2_out));
  Subtractor #(.width(32)) subtractor_2 (.a(shifter_2_out), .b(32'h1), .out(subtractor_2_out));  // open: bin, bout
  Divider divider_2 ();  // open: a, b, out, upper, rem
  Comparator #(.width(32)) comparator_1 (.a(bit_extender_5_out), .b(32'h1), .eq(comparator_1_eq));  // open: gt, lt
  Comparator #(.width(32)) comparator_2 (.a(ALU_Y), .b({32{1'b0}}), .gt(comparator_2_gt));  // open: eq, lt
  Shifter #(.width(32)) shifter_3 (.in(ALU_X), .\dist (bit_extender_1_out), .out(shifter_3_out));
  Multiplexer #(.width(32), .enable("false")) multiplexer_1 (
    .in0({32{1'b0}}), .in1(subtractor_2_out), .out(multiplexer_1_out), .sel(and_2_out));
  and and_2 (and_2_out, comparator_1_eq, comparator_2_gt);
  Adder #(.width(32)) adder_2 (.a(shifter_3_out), .b(multiplexer_1_out), .out(_00_SL));  // open: cin, cout
  Multiplexer #(.select(4), .width(32), .enable("false")) multiplexer_2 (
    .in0(_00_SL), .in1(_01_SR), .in2(_02_And), .in3(_03_OR), .in4(_04_REV), .in5(_05_XOR), .in6(_06_ADD),
    .in7(_07_SUB), .in8(_08_MUL), .in9(_09_DIV), .in10(_06_ADD), .in11(_06_ADD), .in12(_06_ADD),
    .in13(_06_ADD), .in14({ALU_Y[16:0], ALU_X[14:0]}), .out(ALU_RESULT), .sel(ALU_CONTROL));  // open: in15

  // Other names for the same wires on the sheet: _14_STU[31:0] = {ALU_Y[16:0], ALU_X[14:0]}; X[31:0] = ALU_X;
  //   Y[31:0] = ALU_Y
endmodule

// Data Memory
module u_MEM (
  input  [24:0] ADDRESS,
  input  WORD_MODE,
  input  MEM_WRITE,
  input  [31:0] DATA_IN,
  input  CLOCK,
  output [31:0] DATA_OUT
);


  // Notes on the sheet:
  //   Feel free to use this component, or not, however you want!
  //   You might use the word mode input to differentiate LW/SW from LH/SH.
  //   However, you *SHOULD* use 2 RAM modules, one for even addresses and one for odd addresses.
endmodule

module u_REV (
  input  [4:0] REVERSE_AMOUNT,
  input  [31:0] INPUT,
  output [31:0] OUTPUT
);

  wire [31:0] multiplexer_1_out, multiplexer_2_out, multiplexer_3_out, multiplexer_4_out;

  Multiplexer #(.width(32), .enable("false")) multiplexer_1 (
    .in0(INPUT),
    .in1({INPUT[30], INPUT[31], INPUT[28], INPUT[29], INPUT[26], INPUT[27], INPUT[24], INPUT[25], INPUT[22], INPUT[23], INPUT[20], INPUT[21], INPUT[18], INPUT[19], INPUT[16], INPUT[17], INPUT[14], INPUT[15], INPUT[12], INPUT[13], INPUT[10], INPUT[11], INPUT[8], INPUT[9], INPUT[6], INPUT[7], INPUT[4], INPUT[5], INPUT[2], INPUT[3], INPUT[0], INPUT[1]}),
    .out(multiplexer_1_out), .sel(REVERSE_AMOUNT[0]));
  Multiplexer #(.width(32), .enable("false")) multiplexer_2 (
    .in0(multiplexer_1_out),
    .in1({multiplexer_1_out[29:28], multiplexer_1_out[31:30], multiplexer_1_out[25:24], multiplexer_1_out[27:26], multiplexer_1_out[21:20], multiplexer_1_out[23:22], multiplexer_1_out[17:16], multiplexer_1_out[19:18], multiplexer_1_out[13:12], multiplexer_1_out[15:14], multiplexer_1_out[9:8], multiplexer_1_out[11:10], multiplexer_1_out[5:4], multiplexer_1_out[7:6], multiplexer_1_out[1:0], multiplexer_1_out[3:2]}),
    .out(multiplexer_2_out), .sel(REVERSE_AMOUNT[1]));
  Multiplexer #(.width(32), .enable("false")) multiplexer_3 (
    .in0(multiplexer_2_out),
    .in1({multiplexer_2_out[26], multiplexer_2_out[27], multiplexer_2_out[24], multiplexer_2_out[25], multiplexer_2_out[30], multiplexer_2_out[31], multiplexer_2_out[28], multiplexer_2_out[29], multiplexer_2_out[18], multiplexer_2_out[19], multiplexer_2_out[16], multiplexer_2_out[17], multiplexer_2_out[22], multiplexer_2_out[23], multiplexer_2_out[20], multiplexer_2_out[21], multiplexer_2_out[10], multiplexer_2_out[11], multiplexer_2_out[8], multiplexer_2_out[9], multiplexer_2_out[14], multiplexer_2_out[15], multiplexer_2_out[12], multiplexer_2_out[13], multiplexer_2_out[2], multiplexer_2_out[3], multiplexer_2_out[0], multiplexer_2_out[1], multiplexer_2_out[6], multiplexer_2_out[7], multiplexer_2_out[4], multiplexer_2_out[5]}),
    .out(multiplexer_3_out), .sel(REVERSE_AMOUNT[2]));
  Multiplexer #(.width(32), .enable("false")) multiplexer_4 (
    .in0(multiplexer_3_out),
    .in1({multiplexer_3_out[23:16], multiplexer_3_out[31:24], multiplexer_3_out[7:0], multiplexer_3_out[15:8]}),
    .out(multiplexer_4_out), .sel(REVERSE_AMOUNT[3]));
  Multiplexer #(.width(32), .enable("false")) multiplexer_5 (
    .in0(multiplexer_4_out), .in1({multiplexer_4_out[15:0], multiplexer_4_out[31:16]}), .out(OUTPUT),
    .sel(REVERSE_AMOUNT[4]));

  // Other names for the same wires on the sheet: rev_0 = REVERSE_AMOUNT[0]; rev_1 = REVERSE_AMOUNT[1];
  //   rev_2 = REVERSE_AMOUNT[2]; rev_3 = REVERSE_AMOUNT[3]; rev_4 = REVERSE_AMOUNT[4]
endmodule

module u_decode (
  input  [31:0] in_1,
  output [3:0] OP,
  output [2:0] JC,
  output I,
  output [4:0] RD,
  output [4:0] RS,
  output [4:0] RI,
  output [16:0] Immediate,
  output [23:0] Addr
);


  assign Addr = in_1[23:0];
  assign I = in_1[27];
  assign Immediate = in_1[16:0];
  assign JC = in_1[26:24];
  assign OP = in_1[31:28];
  assign RD = in_1[26:22];
  assign RI = in_1[4:0];
  assign RS = in_1[21:17];

  // Other names for the same wires on the sheet: Inst[31:0] = in_1
endmodule

module u_control (
  input  [3:0] OP,
  input  [2:0] JC,
  input  I,
  input  [31:0] JC_2,
  output [3:0] ALU_Control,
  output ALU_Src,
  output J_Src
);


  assign ALU_Control = OP;
  assign ALU_Src = I;
  assign J_Src = I;
endmodule
